// Logisim project 2 BIT ALU.circ as structural Verilog: 2 circuits, main circuit main
module _1_bit_alu (
  input  SUB,
  input  Cin,
  input  A,
  input  B,
  input  INV,
  input  [2:0] in_6,
  output out_7,
  output Cout,
  output out_9
);

  // main main_1: pin names not known; wires that end beside it: SUB, A, Cin, B, B, in_6, INV, out_7, out_9
  // main main_2: pin names not known; wires that end beside it: SUB, A, Cin, B, B, in_6, INV, out_7, Cout

  // Notes on the sheet:
  //   Cout
endmodule

module main (
  input  [2:0] in_1,
  input  [1:0] A,
  input  [1:0] B,
  input  [1:0] inverter,
  output [1:0] out_5
);

  wire comparator_1_eq, comparator_1_gt, comparator_1_lt;
  wire [1:0] adder_1_out, adder_2_out, and_1_out, and_2_out, divider_1_out, divider_2_out, multiplier_1_out,
       multiplier_2_out, nor_1_out, nor_2_out, not_1_out, or_1_out, or_2_out, xor_1_out, xor_2_out;

  assign not_1_out = ~inverter;  // NOT_Gate not_1, 2 bits wide
  assign and_1_out = A & B;  // AND_Gate and_1, 2 bits wide
  assign or_1_out = A | B;  // OR_Gate or_1, 2 bits wide
  assign xor_1_out = A ^ B;  // XOR_Gate xor_1, 2 bits wide
  assign nor_1_out = ~(A | B);  // NOR_Gate nor_1, 2 bits wide
  Comparator #(.width(2)) comparator_1 (.a(A), .b(B), .gt(comparator_1_gt), .eq(comparator_1_eq), .lt(comparator_1_lt));
  Multiplier #(.width(2)) multiplier_1 (.a(A), .b(B), .out(multiplier_1_out));  // open: cin, cout
  Divider #(.width(2)) divider_1 (.a(A), .b(B), .out(divider_1_out));  // open: upper, rem
  Adder #(.width(2)) adder_1 (.a(A), .b(B), .out(adder_1_out));  // open: cin, cout
  assign and_2_out = A & B;  // AND_Gate and_2, 2 bits wide
  assign or_2_out = A | B;  // OR_Gate or_2, 2 bits wide
  assign xor_2_out = A ^ B;  // XOR_Gate xor_2, 2 bits wide
  assign nor_2_out = ~(A | B);  // NOR_Gate nor_2, 2 bits wide
  Multiplier #(.width(2)) multiplier_2 (.a(A), .b(B), .out(multiplier_2_out));  // open: cin, cout
  Divider #(.width(2)) divider_2 (.a(A), .b(B), .out(divider_2_out));  // open: upper, rem
  Adder #(.width(2)) adder_2 (.a(A), .b(B), .out(adder_2_out));  // open: cin, cout
  Multiplexer #(.select(3), .width(2)) multiplexer_1 (
    .in0(and_1_out), .in1(or_1_out), .in2(xor_1_out), .in3(nor_1_out), .in4(adder_1_out), .in5(not_1_out),
    .in6(multiplier_1_out), .in7(divider_1_out), .out(out_5), .sel(in_1));  // open: en
  Multiplexer #(.select(3), .width(2)) multiplexer_2 (
    .in0(and_2_out), .in1(or_2_out), .in2(xor_2_out), .in3(nor_2_out), .in4(adder_2_out), .in5(not_1_out),
    .in6(multiplier_2_out), .in7(divider_2_out), .out(out_5), .sel(in_1));  // open: en
  LED A_B (.in(comparator_1_gt));
  LED A_B_2 (.in(comparator_1_eq));
  LED A_B_3 (.in(comparator_1_lt));

  // Notes on the sheet:
  //   A<B
  //   A=B
  //   A>B
  //   001 -OR
  //   multiplexer input 
  //   000 - AND 
  //   010 -XOR
  //   011 -NOR
  //   100 - Adder
  //   110 -Multiplication
  //   111 -Division
  //   101 -inverter(NOT operation)
endmodule
